// Logisim project MULTIPLEXADOR.circ as structural Verilog: 1 circuit, main circuit main
module main (
  input  in_1,
  input  in_2,
  input  in_3,
  input  in_4,
  input  in_5,
  input  in_6,
  input  in_7,
  input  in_8,
  input  in_9
);

  wire [3:0] multiplexer_1_out;

  LED led_1 (.in(multiplexer_1_out[3]));
  Multiplexer #(.width(4)) multiplexer_1 (
    .in0({in_1, in_2, in_3, in_4}), .in1({in_5, in_6, in_7, in_8}), .out(multiplexer_1_out), .sel(in_9));  // open: en
  LED led_2 (.in(multiplexer_1_out[0]));
  LED led_3 (.in(multiplexer_1_out[2]));
  LED led_4 (.in(multiplexer_1_out[1]));
endmodule
