// Logisim project PROCESSADOR COM ROM1.circ as structural Verilog: 1 circuit, main circuit main
module main (
);

  wire and_1_out, and_2_out, clock_1_out, not_1_out;
  wire [1:0] counter_1_q;
  wire [4:0] adder_1_out, multiplexer_1_out, multiplexer_2_out, register_1_q, register_2_q;
  wire [8:0] rom_1_data;

  ROM #(.addrWidth(2), .dataWidth(9)) rom_1 (.addr(counter_1_q), .data(rom_1_data));  // open: sel
  Counter #(.width(2), .max('h3)) counter_1 (.Q(counter_1_q), .clk(clock_1_out));  // open: load, D, count, carry, clr
  Clock clock_1 (.out(clock_1_out));
  not not_1 (not_1_out, clock_1_out);
  and and_1 (and_1_out, rom_1_data[6], not_1_out);
  and and_2 (and_2_out, rom_1_data[5], not_1_out);
  LED led_1 (.in(register_1_q[4]));
  LED led_2 (.in(register_1_q[2]));
  LED led_3 (.in(register_1_q[1]));
  LED led_4 (.in(register_1_q[0]));
  LED led_5 (.in(register_1_q[3]));
  Register #(.width(5), .trigger("falling")) register_1 (
    .D(adder_1_out), .Q(register_1_q), .clk(and_1_out));  // open: en, clr
  Register #(.width(5), .trigger("falling")) register_2 (
    .D(adder_1_out), .Q(register_2_q), .clk(and_2_out));  // open: en, clr
  LED led_6 (.in(register_2_q[4]));
  LED led_7 (.in(register_2_q[3]));
  LED led_8 (.in(register_2_q[2]));
  LED led_9 (.in(register_2_q[1]));
  LED led_10 (.in(register_2_q[0]));
  Multiplexer #(.width(5)) multiplexer_1 (
    .in0(rom_1_data[4:0]), .in1(register_1_q), .out(multiplexer_1_out), .sel(rom_1_data[7]));  // open: en
  Multiplexer #(.width(5)) multiplexer_2 (
    .in0({5{1'b0}}), .in1(register_2_q), .out(multiplexer_2_out), .sel(rom_1_data[8]));  // open: en
  Adder #(.width(5)) adder_1 (
    .a(multiplexer_1_out), .b(multiplexer_2_out), .out(adder_1_out), .cin(1'b0));  // open: cout

  // Notes on the sheet:
  //   contents of rom_1 (hex, n*v repeats v):
  //   24 1a 1ff 30
endmodule
