// Logisim project PROCESSADOR r10 .circ as structural Verilog: 1 circuit, main circuit main
module main (
  input  in_1,
  input  in_2,
  input  in_3,
  input  in_4,
  input  in_5,
  input  in_6,
  input  in_7,
  input  in_8,
  input  in_9,
  input  in_10
);

  wire and_1_out, and_2_out, clock_1_out;
  wire [4:0] adder_1_out, multiplexer_1_out, multiplexer_2_out, multiplexer_3_out, multiplier_1_out,
       register_1_q, register_2_q;

  Clock clock_1 (.out(clock_1_out));
  and and_1 (and_1_out, in_3, clock_1_out);
  and and_2 (and_2_out, in_4, clock_1_out);
  LED led_1 (.in(register_1_q[3]));
  LED led_2 (.in(register_1_q[4]));
  LED led_3 (.in(register_1_q[0]));
  LED led_4 (.in(register_1_q[1]));
  LED led_5 (.in(register_1_q[2]));
  Register #(.width(5), .trigger("falling")) register_1 (
    .D(multiplexer_3_out), .Q(register_1_q), .clk(and_1_out));  // open: en, clr
  Register #(.width(5), .trigger("falling")) register_2 (
    .D(multiplexer_3_out), .Q(register_2_q), .clk(and_2_out));  // open: en, clr
  LED led_6 (.in(register_2_q[1]));
  LED led_7 (.in(register_2_q[2]));
  LED led_8 (.in(register_2_q[4]));
  LED led_9 (.in(register_2_q[3]));
  LED led_10 (.in(register_2_q[0]));
  Multiplexer #(.width(5)) multiplexer_1 (
    .in0({in_5, in_6, in_7, in_8, in_9}), .in1(register_1_q), .out(multiplexer_1_out), .sel(in_2));  // open: en
  Multiplexer #(.width(5)) multiplexer_2 (
    .in0({5{1'b0}}), .in1(register_2_q), .out(multiplexer_2_out), .sel(in_1));  // open: en
  Multiplexer #(.width(5)) multiplexer_3 (
    .in0(adder_1_out), .in1(multiplier_1_out), .out(multiplexer_3_out), .sel(in_10));  // open: en
  Adder #(.width(5)) adder_1 (
    .a(multiplexer_1_out), .b(multiplexer_2_out), .out(adder_1_out), .cin(1'b0));  // open: cout
  LED led_11 (.in(multiplier_1_out[4]));
  Multiplier #(.width(5)) multiplier_1 (
    .a(multiplexer_1_out), .b(multiplexer_2_out), .out(multiplier_1_out));  // open: cin, cout
  LED led_12 (.in(multiplier_1_out[3]));
  LED led_13 (.in(multiplier_1_out[1]));
  LED led_14 (.in(multiplier_1_out[2]));
  LED led_15 (.in(multiplier_1_out[0]));
endmodule
