// Logisim project PROCESSADOR.circ as structural Verilog: 1 circuit, main circuit main
module main (
  input  in_1,
  input  in_2,
  input  in_3,
  input  in_4,
  input  in_5,
  input  in_6,
  input  in_7,
  input  in_8,
  input  in_9,
  input  in_10,
  input  in_11,
  input  in_12,
  input  in_13,
  input  in_14,
  input  in_15,
  input  in_16,
  input  in_17,
  input  in_18,
  input  in_19,
  input  in_20,
  input  in_21,
  input  in_22,
  input  in_23,
  input  in_24
);

  wire and_1_out, and_2_out, and_3_out, and_4_out, and_5_out, and_6_out, clock_1_out, clock_2_out,
       clock_3_out;
  wire [3:0] adder_1_out, adder_2_out, multiplexer_1_out, multiplexer_2_out, multiplexer_3_out,
       multiplexer_4_out, multiplexer_5_out, multiplexer_6_out, multiplier_1_out, register_1_q, register_2_q,
       register_3_q, register_4_q, register_5_q, register_6_q, subtractor_1_out;

  Clock clock_1 (.out(clock_1_out));
  Clock clock_2 (.out(clock_2_out));
  Clock clock_3 (.out(clock_3_out));
  and and_1 (and_1_out, in_3, clock_1_out);
  and and_2 (and_2_out, in_4, clock_1_out);
  and and_3 (and_3_out, in_11, clock_2_out);
  and and_4 (and_4_out, in_12, clock_2_out);
  and and_5 (and_5_out, in_19, clock_3_out);
  and and_6 (and_6_out, in_20, clock_3_out);
  LED led_1 (.in(register_1_q[3]));
  LED led_2 (.in(register_3_q[3]));
  LED led_3 (.in(register_5_q[3]));
  LED led_4 (.in(register_1_q[1]));
  LED led_5 (.in(register_1_q[2]));
  LED led_6 (.in(register_1_q[0]));
  Register #(.width(4), .trigger("falling")) register_1 (
    .D(adder_1_out), .Q(register_1_q), .clk(and_1_out));  // open: en, clr
  Register #(.width(4), .trigger("falling")) register_2 (
    .D(adder_1_out), .Q(register_2_q), .clk(and_2_out));  // open: en, clr
  LED led_7 (.in(register_3_q[1]));
  LED led_8 (.in(register_3_q[2]));
  LED led_9 (.in(register_3_q[0]));
  Register #(.width(4), .trigger("falling")) register_3 (
    .D(subtractor_1_out), .Q(register_3_q), .clk(and_3_out));  // open: en, clr
  Register #(.width(4), .trigger("falling")) register_4 (
    .D(subtractor_1_out), .Q(register_4_q), .clk(and_4_out));  // open: en, clr
  LED led_10 (.in(register_5_q[1]));
  LED led_11 (.in(register_5_q[2]));
  LED led_12 (.in(register_5_q[0]));
  Register #(.width(4), .trigger("falling")) register_5 (
    .D(adder_2_out), .Q(register_5_q), .clk(and_5_out));  // open: en, clr
  Register #(.width(4), .trigger("falling")) register_6 (
    .D(adder_2_out), .Q(register_6_q), .clk(and_6_out));  // open: en, clr
  LED led_13 (.in(register_2_q[1]));
  LED led_14 (.in(register_2_q[2]));
  LED led_15 (.in(register_2_q[3]));
  LED led_16 (.in(register_4_q[1]));
  LED led_17 (.in(register_4_q[3]));
  LED led_18 (.in(register_4_q[2]));
  LED led_19 (.in(register_6_q[1]));
  LED led_20 (.in(register_6_q[2]));
  LED led_21 (.in(register_6_q[3]));
  LED led_22 (.in(register_2_q[0]));
  LED led_23 (.in(register_4_q[0]));
  LED led_24 (.in(register_6_q[0]));
  Multiplexer #(.width(4)) multiplexer_1 (
    .in0({in_5, in_6, in_7, in_8}), .in1(register_1_q), .out(multiplexer_1_out), .sel(in_2));  // open: en
  Multiplexer #(.width(4)) multiplexer_2 (
    .in0(4'b0000), .in1(register_2_q), .out(multiplexer_2_out), .sel(in_1));  // open: en
  Multiplexer #(.width(4)) multiplexer_3 (
    .in0({in_13, in_14, in_15, in_16}), .in1(register_3_q), .out(multiplexer_3_out), .sel(in_10));  // open: en
  Multiplexer #(.width(4)) multiplexer_4 (
    .in0(4'b0000), .in1(register_4_q), .out(multiplexer_4_out), .sel(in_9));  // open: en
  Multiplexer #(.width(4)) multiplexer_5 (
    .in0({in_21, in_22, in_23, in_24}), .in1(register_5_q), .out(multiplexer_5_out), .sel(in_18));  // open: en
  Multiplexer #(.width(4)) multiplexer_6 (
    .in0(4'b0000), .in1(register_6_q), .out(multiplexer_6_out), .sel(in_17));  // open: en
  Adder #(.width(4)) adder_1 (
    .a(multiplexer_1_out), .b(multiplexer_2_out), .out(adder_1_out), .cin(1'b0));  // open: cout
  Subtractor #(.width(4)) subtractor_1 (
    .a(multiplexer_3_out), .b(multiplexer_4_out), .out(subtractor_1_out), .bin(1'b0));  // open: bout
  Adder #(.width(4)) adder_2 (
    .a(multiplexer_5_out), .b(multiplexer_6_out), .out(adder_2_out), .cin(1'b0));  // open: cout
  LED led_25 (.in(multiplier_1_out[2]));
  LED led_26 (.in(multiplier_1_out[3]));
  Multiplier #(.width(4)) multiplier_1 (
    .a(multiplexer_5_out), .b(multiplexer_6_out), .out(multiplier_1_out));  // open: cin, cout
  LED led_27 (.in(multiplier_1_out[1]));
  LED led_28 (.in(multiplier_1_out[0]));
endmodule
