// Logisim project REGISTRADOR.circ as structural Verilog: 1 circuit, main circuit main
module main (
  input  in_1,
  input  in_2,
  input  in_3,
  input  in_4,
  input  in_5
);

  wire [3:0] register_1_q;

  Register #(.width(4)) register_1 (.D({in_4, in_3, in_2, in_1}), .Q(register_1_q), .clk(in_5));  // open: en, clr
  LED led_1 (.in(register_1_q[0]));
  LED led_2 (.in(register_1_q[1]));
  LED led_3 (.in(register_1_q[2]));
  LED led_4 (.in(register_1_q[3]));
endmodule
