// Logisim project SOMADOR.circ as structural Verilog: 1 circuit, main circuit main
module main (
  input  in_1,
  input  in_2,
  input  in_3,
  input  in_4,
  input  in_5,
  input  in_6,
  input  in_7,
  input  in_8
);

  wire adder_1_cout;
  wire [3:0] adder_1_out;

  LED led_1 (.in(adder_1_out[3]));
  LED led_2 (.in(adder_1_cout));
  Adder #(.width(4)) adder_1 (
    .a({in_5, in_6, in_7, in_8}), .b({in_1, in_2, in_3, in_4}), .out(adder_1_out), .cout(adder_1_cout));  // open: cin
  LED led_3 (.in(adder_1_out[0]));
  LED led_4 (.in(adder_1_out[2]));
  LED led_5 (.in(adder_1_out[1]));
endmodule
